// Logisim project Ejercicio1.circ as structural Verilog: 1 circuit, main circuit main
module main (
  input  A,
  input  B,
  input  C,
  output Z
);

  wire not_1_out;

  not not_1 (not_1_out, A);
  and and_1 (Z, not_1_out, B, C);
endmodule
