// Logisim project Ejercicio2.circ as structural Verilog: 1 circuit, main circuit main
module main (
  input  A,
  input  B,
  input  C,
  output Z0,
  output Z1
);

  wire not_1_out, not_2_out, not_3_out;

  not not_1 (not_1_out, A);
  not not_2 (not_2_out, C);
  not not_3 (not_3_out, A);
  and and_1 (Z0, not_1_out, B, not_2_out);
  and and_2 (Z1, not_3_out, B, C);
endmodule
