// Logisim project Ejercicio3.circ as structural Verilog: 1 circuit, main circuit main
module main (
  input  A,
  input  B,
  input  C,
  output out_4,
  output out_5,
  output out_6,
  output out_7,
  output out_8,
  output out_9,
  output out_10,
  output out_11
);

  wire not_1_out, not_2_out, not_3_out, not_4_out, not_5_out, not_6_out, not_7_out, not_8_out, not_9_out,
       not_10_out, not_11_out, not_12_out;

  not not_1 (not_1_out, A);
  not not_2 (not_2_out, B);
  not not_3 (not_3_out, C);
  not not_4 (not_4_out, A);
  not not_5 (not_5_out, B);
  not not_6 (not_6_out, A);
  not not_7 (not_7_out, C);
  not not_8 (not_8_out, A);
  not not_9 (not_9_out, B);
  not not_10 (not_10_out, C);
  not not_11 (not_11_out, B);
  not not_12 (not_12_out, C);
  and and_1 (out_4, not_1_out, not_2_out, not_3_out);
  and and_2 (out_5, not_4_out, not_5_out, C);
  and and_3 (out_6, not_6_out, B, not_7_out);
  and and_4 (out_7, not_8_out, B, C);
  and and_5 (out_8, A, not_9_out, not_10_out);
  and and_6 (out_9, A, not_11_out, C);
  and and_7 (out_10, A, B, not_12_out);
  and and_8 (out_11, A, B, C);

  // Notes on the sheet:
  //   Z0
  //   Z1
  //   Z2
  //   Z3
  //   Z4
  //   Z5
  //   Z6
  //   Z7
endmodule
